# Fritzing sketch Spod3Fritzing (saved by Fritzing 1.0.0rc)
breadboards: 2

parts:
  Part1 = Arduino Nano (Rev3.0) (ICSP)
  LLC1 = Logic Level Converter [package="Breakout board"]  # not connected
  LLC2 = Logic Level Converter [package="Breakout board"]  # not connected
  R1 = Resistor [tolerance=±1% resistance=10000 package="1206 [SMD]"]
  R2 = Resistor [tolerance=±1% resistance=10000 package="1206 [SMD]"]
  R3 = Resistor [tolerance=±1% resistance=10000 package="1206 [SMD]"]
  R4 = Resistor [tolerance=±1% resistance=10000 package="1206 [SMD]"]
  R5 = Resistor [tolerance=±1% resistance=10000 package="1206 [SMD]"]
  R6 = Resistor [tolerance=±1% resistance=10000 package="1206 [SMD]"]
  Part2 = Adafruit BME680  # not connected
  Mod1 = MQ-7 breakout
  Mod2 = MQ-7 breakout
  Mod3 = MQ-7 breakout
  Mod4 = MQ-7 breakout
  Mod5 = MQ-7 breakout
  Mod6 = MQ-7 breakout

nets:
  N1: Part1.GND, Mod1.AO, Mod2.AO, Mod3.AO, Mod4.AO, Mod5.AO, Mod6.AO
  N2: R1.Pin_0, R2.Pin_0, R3.Pin_0, R4.Pin_0, R5.Pin_0, R6.Pin_0, Mod1.DO, Mod2.DO, Mod3.DO, Mod4.DO, Mod5.DO, Mod6.DO
  N3: R1.Pin_1, Mod1.VCC
  N4: R2.Pin_1, Mod2.VCC
  N5: R3.Pin_1, Mod3.VCC
  N6: R4.Pin_1, Mod4.VCC
  N7: R5.Pin_1, Mod5.VCC

notes:
  5V
  3.3V
  A0-Yellow
  A1-Orange
  A2-Cyan
  A3-Purple
  A4-Brown
  A5-Ochra

custom parts:
  Logic Level Converter: 5V to/from 3.3V logic level converter
  MQ-7 breakout: MQ-5 gas sensor
